// Logisim project reti_logiche.circ as structural Verilog
module mux_2to1 (
  input  x1,
  input  x0,
  input  b0,
  output z
);

  wire and_1_out, and_2_out, not_1_out;

  not not_1 (not_1_out, b0);
  and and_1 (and_1_out, x1, b0);
  and and_2 (and_2_out, x0, not_1_out);
  or or_1 (z, and_1_out, and_2_out);
endmodule

module mux_4to1 (
  input  x3,
  input  x2,
  input  x1,
  input  x0,
  input  b1,
  input  b0,
  output z
);

  wire mux_2to1_1_z, mux_2to1_2_z;

  mux_2to1 mux_2to1_1 (.x1(x3), .x0(x2), .b0(b0), .z(mux_2to1_1_z));
  mux_2to1 mux_2to1_2 (.x1(x1), .x0(x0), .b0(b0), .z(mux_2to1_2_z));
  mux_2to1 mux_2to1_3 (.x1(mux_2to1_1_z), .x0(mux_2to1_2_z), .b0(b1), .z(z));
endmodule

module demux_1to2 (
  input  x,
  input  b0,
  output z1,
  output z0
);

  wire not_1_out;

  not not_1 (not_1_out, b0);
  and and_1 (z1, x, b0);
  and and_2 (z0, x, not_1_out);
endmodule

module demux_1to4 (
  input  x,
  input  b1,
  input  b0,
  output z3,
  output z2,
  output z1,
  output z30
);

  wire demux_1to2_1_z0, demux_1to2_1_z1;

  demux_1to2 demux_1to2_1 (.x(x), .b0(b1), .z1(demux_1to2_1_z1), .z0(demux_1to2_1_z0));
  demux_1to2 demux_1to2_2 (.x(demux_1to2_1_z1), .b0(b0), .z1(z3), .z0(z2));
  demux_1to2 demux_1to2_3 (.x(demux_1to2_1_z0), .b0(b0), .z1(z1), .z0(z30));
endmodule

module sr_latch (
  input  s,
  input  r,
  output qn,
  output q
);

  nor nor_1 (qn, s, q);
  nor nor_2 (q, r, qn);
endmodule

module full_sr_latch (
  input  s,
  input  r,
  input  preset,
  input  preclear,
  output qn,
  output q
);

  wire and_1_out, and_2_out, not_1_out, not_2_out, or_1_out, or_2_out;

  not not_1 (not_1_out, preset);
  not not_2 (not_2_out, preclear);
  and and_1 (and_1_out, s, preclear);
  or or_1 (or_1_out, and_1_out, not_1_out);
  and and_2 (and_2_out, r, preset);
  or or_2 (or_2_out, and_2_out, not_2_out);
  sr_latch sr_latch_1 (.s(or_1_out), .r(or_2_out), .qn(qn), .q(q));
endmodule
